# Fritzing sketch SensorSchema (saved by Fritzing 0.9.3b)

parts:
  Part1 = Arduino Nano (Rev3.0)
  U1 = TCRT5000 [package=THT]
  R1 = Resistor [tolerance=±5% resistance=10k package=THT]
  R2 = Resistor [tolerance=±5% resistance=500 package=THT]

nets:
  N1: Part1.GND, R1.Pin_1, R2.Pin_0
  N2: Part1.5V, U1.Pin_1, U1.Pin_4
  N3: Part1.A0, U1.Pin_2, R1.Pin_0
  N4: U1.Pin_3, R2.Pin_1

notes:
  Transistor is black
  Diode is blue

custom parts:
  TCRT5000: TCRT5000 optical reflective sensor
